# Fritzing sketch basket_schematic (saved by Fritzing 0.9.3b)
breadboards: 1

parts:
  Part1 = Photon
  S1 = SWITCH-MOMENTARY-2 [package=tactile-pth-12mm]

nets:
  N1: Part1.D3, S1.1
  N2: Part1.3V3, S1.2
