# Fritzing sketch discbit_schematic (saved by Fritzing 0.9.3b)
breadboards: 1

parts:
  Part1 = Photon
  Part2 = Adafruit Bluefruit LE UART Friend [part_number="Adafruit #2479"]

nets:
  N1: Part1.RX, Part2.TXO
  N2: Part1.TX, Part2.RXI
  GND: Part1.GND, Part2.GND, Part2.CTS
  N3: Part1.D2, Part2.MODE
  3V3: Part1.3V3, Part2.VIN

custom parts:
  Adafruit Bluefruit LE UART Friend: The Bluefruit LE UART Friend makes it easy to add Bluetooth Low Energy connectivity to anything with a hardware or software serial port. We even have nice hardware flow control so you won't have to think about losing data. Connect to your Arduino or other microcontroller or even just a standard FTDI cable for debugging and testing.
